# Fritzing sketch Gleisbesetzmeldung (saved by Fritzing 0.9.3b)
breadboards: 1

parts:
  IC1 = IC, DIP package, 6 pins [chip_label=IC part_number=CNY-17-2]
  Q1 = NPN-Transistor [part_number=2N2222 package="TO92 [THT]"]
  R2 = Resistor [tolerance=±5% resistance=1k package=THT]
  R1 = Resistor [tolerance=±5% resistance=1k package=THT]
  JP4 = Header 2 [package=molex-1x2_lock]
  D1 = Diode [package=diode-1n4001]
  D2 = Diode [package=diode-1n4001]
  D3 = Diode [package=diode-1n4001]
  D4 = Diode [package=diode-1n4001]
  JP3 = Header 2 [package=molex-1x2_lock]
  C1 = Electrolytic Capacitor [capacitance=4.7mF voltage=35V package="200 mil [THT, electrolytic]"]

nets (from the schematic view):
  N1: IC1.pin1, R1.Pin_1
  N2: IC1.pin2, D2.A, D3.A, C1.-
  GND: IC1.pin4, Q1.E
  N3: IC1.pin5, Q1.B, R2.Pin_0
  5V: Q1.C, R2.Pin_1, JP4.1
  N4: R1.Pin_0, D1.C, D4.C
  N5: D1.A, D2.C, JP3.1
  N6: D3.C, D4.A, JP3.2
